// Logisim project CPU.circ as structural Verilog: 8 circuits, main circuit main
module main (
  input  reset,
  output MemWrite,
  output RegWrite,
  output [31:0] instar,
  output [4:0] RegAddr,
  output [31:0] MemAddr,
  output [31:0] PC,
  output [31:0] RegData,
  output [31:0] MemData
);

  wire BSel, clk, extlu, npcop, WDsel, WRsel, zero;
  wire [1:0] EXTop;
  wire [2:0] ALUop;
  wire [7:0] counter_1_q;
  wire [15:0] offest;
  wire [25:0] imm26;
  wire [31:0] DMRD, EXTout, multiplexer_1_out, multiplexer_3_out, npc, PC_t, RD1;

  Clock clock_1 (.out(clk));
  // Probe on instar[31:26]
  // Probe on instar[5:0]
  // Probe on instar
  IFU ifu_1 (.PC(npc), .clk(clk), .instr(instar), .clr(reset), ._15_0(offest), .PCnew(PC_t), ._25_00(imm26));
  Extd extd_1 (.imm(offest), .O(EXTout), .set(EXTop));
  Counter #(.ongoal("stay")) counter_1 (.Q(counter_1_q), .clk(clk));  // open: load, D, count, carry, clr
  // Probe on counter_1_q
  control control_1 (
    ._31_26(instar[31:26]), ._5_0(instar[5:0]), .EXTop(EXTop), .WDsel(WDsel), .ALUop(ALUop), .WRsel(WRsel),
    .NPCop(npcop), .exttoalu(extlu), .DMwr(MemWrite), .BSsel(BSel), .RFWE(RegWrite));
  // Probe on instar[25:21]
  // Probe on instar[20:16]
  Adder #(.width(32)) adder_1 (.a(32'h3000), .b(PC_t), .out(PC));  // open: cin, cout
  // Probe on instar
  // Probe on PC
  NPC npc_1 (.PC(PC_t), .imm(imm26), .s1(RD1), .NPC(npc), .op(npcop), .ZERO(zero));  // open: nextPC
  Multiplexer #(.width(32), .enable("false")) multiplexer_1 (
    .in0(MemData), .in1(EXTout), .out(multiplexer_1_out), .sel(BSel));
  // Probe on RegData
  Multiplexer #(.width(5), .enable("false")) multiplexer_2 (
    .in0(instar[15:11]), .in1(instar[20:16]), .out(RegAddr), .sel(WRsel));
  Multiplexer #(.width(32), .enable("false")) multiplexer_3 (
    .in0(MemAddr), .in1(EXTout), .out(multiplexer_3_out), .sel(extlu));
  ALU alu_1 (.A(RD1), .B(multiplexer_1_out), .C(MemAddr), .F(ALUop), .eq(zero));  // open: ad
  Multiplexer #(.width(32), .enable("false")) multiplexer_4 (
    .in0(DMRD), .in1(multiplexer_3_out), .out(RegData), .sel(WDsel));
  GRF grf_1 (
    .A1(instar[25:21]), .A2(instar[20:16]), .A3(RegAddr), .WD(RegData), .RD1(RD1), .RD2(MemData),
    .reset(reset), .WE(RegWrite), .clk(clk));
  DM dm_1 (.ADDR(MemAddr), .WD(MemData), .out_6(DMRD), .WR(MemWrite), .clk(clk), .clr(reset));

  // Other names for the same wires on the sheet: ALUout[31:0] = MemAddr; DMaddr[31:0] = MemAddr; DMwr = MemWrite;
  //   rd[4:0] = instar[15:11]; rt[4:0] = instar[20:16]; rs[4:0] = instar[25:21]; PC3[31:0] = PC;
  //   DMdata[31:0] = MemData; RD2[31:0] = MemData; RFWE = RegWrite

  // Notes on the sheet:
  //   上次对rd2的修改使原本sw写入错误，违背了不改动原本电路的原则
  //   不能把非最终端口信号直接作为输出，假如端口调整，导致输出无法及时调整
endmodule

module GRF (
  input  clk,
  input  reset,
  input  WE,
  input  [4:0] A1,
  input  [4:0] A2,
  input  [4:0] A3,
  input  [31:0] WD,
  output [31:0] RD1,
  output [31:0] RD2
);

  wire [31:0] demultiplexer_1_out0, i1, i2, i3, i4, i5, i6, i7, i8, i9, i10, i11, i12, i13, i14, i15, i16,
       i17, i18, i19, i20, i21, i22, i23, i24, i25, i26, i27, i28, i29, i30, i31, o0, o1, o2, o3, o4, o5, o6,
       o7, o8, o9, o10, o11, o12, o13, o14, o15, o16, o17, o18, o19, o20, o21, o22, o23, o24, o25, o26, o27,
       o28, o29, o30, o31;

  // Probe on i1
  // Probe on demultiplexer_1_out0
  Demultiplexer #(.select(5), .width(32), .tristate("true")) demultiplexer_1 (
    .out0(demultiplexer_1_out0), .out1(i1), .out2(i2), .out3(i3), .out4(i4), .out5(i5), .out6(i6), .out7(i7),
    .out8(i8), .out9(i9), .out10(i10), .out11(i11), .out12(i12), .out13(i13), .out14(i14), .out15(i15),
    .out16(i16), .out17(i17), .out18(i18), .out19(i19), .out20(i20), .out21(i21), .out22(i22), .out23(i23),
    .out24(i24), .out25(i25), .out26(i26), .out27(i27), .out28(i28), .out29(i29), .out30(i30), .out31(i31),
    .in(WD), .sel(A3), .en(WE));
  Register #(.width(32)) register_1 (.D({32{1'b0}}), .Q(o0), .clk(clk), .clr(reset));  // open: en
  Register #(.width(32)) register_2 (.D(i8), .Q(o8), .clk(clk), .clr(reset));  // open: en
  Register #(.width(32)) register_3 (.D(i16), .Q(o16), .clk(clk), .clr(reset));  // open: en
  Register #(.width(32)) register_4 (.D(i24), .Q(o24), .clk(clk), .clr(reset));  // open: en
  Register #(.width(32)) register_5 (.D(i1), .Q(o1), .clk(clk), .clr(reset));  // open: en
  Register #(.width(32)) register_6 (.D(i9), .Q(o9), .clk(clk), .clr(reset));  // open: en
  Register #(.width(32)) register_7 (.D(i17), .Q(o17), .clk(clk), .clr(reset));  // open: en
  Register #(.width(32)) register_8 (.D(i25), .Q(o25), .clk(clk), .clr(reset));  // open: en
  Register #(.width(32)) register_9 (.D(i2), .Q(o2), .clk(clk), .clr(reset));  // open: en
  Register #(.width(32)) register_10 (.D(i10), .Q(o10), .clk(clk), .clr(reset));  // open: en
  Register #(.width(32)) register_11 (.D(i18), .Q(o18), .clk(clk), .clr(reset));  // open: en
  Register #(.width(32)) register_12 (.D(i26), .Q(o26), .clk(clk), .clr(reset));  // open: en
  Register #(.width(32)) register_13 (.D(i3), .Q(o3), .clk(clk), .clr(reset));  // open: en
  Register #(.width(32)) register_14 (.D(i11), .Q(o11), .clk(clk), .clr(reset));  // open: en
  Register #(.width(32)) register_15 (.D(i19), .Q(o19), .clk(clk), .clr(reset));  // open: en
  Register #(.width(32)) register_16 (.D(i27), .Q(o27), .clk(clk), .clr(reset));  // open: en
  Multiplexer #(.select(5), .width(32), .enable("false")) multiplexer_1 (
    .in0(o0), .in1(o1), .in2(o2), .in3(o3), .in4(o4), .in5(o5), .in6(o6), .in7(o7), .in8(o8), .in9(o9),
    .in10(o10), .in11(o11), .in12(o12), .in13(o13), .in14(o14), .in15(o15), .in16(o16), .in17(o17),
    .in18(o18), .in19(o19), .in20(o20), .in21(o21), .in22(o22), .in23(o23), .in24(o24), .in25(o25),
    .in26(o26), .in27(o27), .in28(o28), .in29(o29), .in30(o30), .in31(o31), .out(RD1), .sel(A1));
  Register #(.width(32)) register_17 (.D(i4), .Q(o4), .clk(clk), .clr(reset));  // open: en
  Register #(.width(32)) register_18 (.D(i12), .Q(o12), .clk(clk), .clr(reset));  // open: en
  Register #(.width(32)) register_19 (.D(i20), .Q(o20), .clk(clk), .clr(reset));  // open: en
  Register #(.width(32)) register_20 (.D(i28), .Q(o28), .clk(clk), .clr(reset));  // open: en
  Register #(.width(32)) register_21 (.D(i5), .Q(o5), .clk(clk), .clr(reset));  // open: en
  Register #(.width(32)) register_22 (.D(i13), .Q(o13), .clk(clk), .clr(reset));  // open: en
  Register #(.width(32)) register_23 (.D(i21), .Q(o21), .clk(clk), .clr(reset));  // open: en
  Register #(.width(32)) register_24 (.D(i29), .Q(o29), .clk(clk), .clr(reset));  // open: en
  Register #(.width(32)) register_25 (.D(i6), .Q(o6), .clk(clk), .clr(reset));  // open: en
  Register #(.width(32)) register_26 (.D(i14), .Q(o14), .clk(clk), .clr(reset));  // open: en
  Register #(.width(32)) register_27 (.D(i22), .Q(o22), .clk(clk), .clr(reset));  // open: en
  Register #(.width(32)) register_28 (.D(i30), .Q(o30), .clk(clk), .clr(reset));  // open: en
  Register #(.width(32)) register_29 (.D(i7), .Q(o7), .clk(clk), .clr(reset));  // open: en
  Register #(.width(32)) register_30 (.D(i15), .Q(o15), .clk(clk), .clr(reset));  // open: en
  Register #(.width(32)) register_31 (.D(i23), .Q(o23), .clk(clk), .clr(reset));  // open: en
  Register #(.width(32)) register_32 (.D(i31), .Q(o31), .clk(clk), .clr(reset));  // open: en
  Multiplexer #(.select(5), .width(32), .enable("false")) multiplexer_2 (
    .in0(o0), .in1(o1), .in2(o2), .in3(o3), .in4(o4), .in5(o5), .in6(o6), .in7(o7), .in8(o8), .in9(o9),
    .in10(o10), .in11(o11), .in12(o12), .in13(o13), .in14(o14), .in15(o15), .in16(o16), .in17(o17),
    .in18(o18), .in19(o19), .in20(o20), .in21(o21), .in22(o22), .in23(o23), .in24(o24), .in25(o25),
    .in26(o26), .in27(o27), .in28(o28), .in29(o29), .in30(o30), .in31(o31), .out(RD2), .sel(A2));
endmodule

module ALU (
  input  [31:0] A,
  input  [31:0] B,
  input  [2:0] F,
  output ad,
  output eq,
  output [31:0] C
);

  wire [31:0] adder_1_out, or_1_out, subtractor_1_out;

  Comparator #(.width(32), .mode("unsigned")) comparator_1 (.a(A), .b(B), .gt(ad), .eq(eq));  // open: lt
  Adder #(.width(32)) adder_1 (.a(A), .b(B), .out(adder_1_out));  // open: cin, cout
  Subtractor #(.width(32)) subtractor_1 (.a(A), .b(B), .out(subtractor_1_out));  // open: bin, bout
  assign or_1_out = A | B;  // OR_Gate or_1, 32 bits wide
  Multiplexer #(.select(3), .width(32), .enable("false")) multiplexer_1 (
    .in0({32{1'b0}}), .in1(adder_1_out), .in2(subtractor_1_out), .in3(or_1_out), .out(C), .sel(F));  // open: in4, in5, in6, in7
endmodule

module Extd (
  input  [1:0] set,
  input  [15:0] imm,
  output [31:0] O
);

  wire [31:0] bit_extender_1_out, bit_extender_2_out;

  assign bit_extender_1_out = {{16{1'b0}}, imm};  // Bit_Extender bit_extender_1
  assign bit_extender_2_out = {{16{imm[15]}}, imm};  // Bit_Extender bit_extender_2
  Multiplexer #(.select(2), .width(32), .enable("false")) multiplexer_1 (
    .in0(bit_extender_1_out), .in1(bit_extender_2_out), .in2({imm, {16{1'b0}}}), .out(O), .sel(set));  // open: in3
endmodule

module DM (
  input  [31:0] ADDR,
  input  clk,
  input  WR,
  input  clr,
  input  [31:0] WD,
  output [31:0] out_6
);

  RAM #(.addrWidth(14), .dataWidth(32), .bus("separate")) ram_1 (
    .addr(ADDR[15:2]), .din(WD), .data(out_6), .str(WR), .clk(clk), .clr(clr));  // open: sel, ld

  // Other names for the same wires on the sheet: address[31:0] = ADDR
endmodule

module IFU (
  input  [31:0] PC,
  input  clk,
  input  clr,
  output [31:0] instr,
  output [25:0] _25_00,
  output [15:0] _15_0,
  output [31:0] PCnew
);

  Register #(.width(32)) register_1 (.D(PC), .Q(PCnew), .clk(clk), .clr(clr));  // open: en
  ROM #(.addrWidth(13), .dataWidth(32)) rom_1 (
    .addr(PCnew[14:2]), .data({instr[31:26], _25_00[25:16], _15_0}));  // open: sel

  assign _25_00[15:0] = _15_0;
  assign instr[25:0] = {_25_00[25:16], _15_0};

  // Notes on the sheet:
  //   contents of rom_1 (hex, n*v repeats v):
  //   341c0000 341d0000 34013456 210820 8c010004 ac010004 3c027878 411822 3c051234 34040005 0 ac85ffff
  //   8c83ffff 10650001 1000000d 34670404 10e3000b 0 3c087777 3508ffff 80022 34001100 e65020 34080000
  //   34090001 340a0001 10a4020 1109fffe 1000ffff
endmodule

module control (
  input  [5:0] _31_26,
  input  [5:0] _5_0,
  output [2:0] ALUop,
  output [1:0] EXTop,
  output exttoalu,
  output WDsel,
  output WRsel,
  output NPCop,
  output DMwr,
  output BSsel,
  output RFWE
);

  wire add_out, beq, lui, lw, not_1_out, not_2_out, not_3_out, not_4_out, not_5_out, not_6_out, not_7_out,
       not_8_out, not_9_out, not_10_out, not_11_out, not_12_out, or_1_out, or_2_out, or_3_out, or_4_out, ori,
       pull_resistor_1_node, special0, sub_out, sw;

  and and_1 (ori, not_1_out, not_2_out, _31_26[3], _31_26[2], not_5_out, _31_26[0]);
  and u_lw (lw, _31_26[5], not_2_out, not_3_out, not_4_out, _31_26[1], _31_26[0]);
  and u_sw (sw, _31_26[5], not_2_out, _31_26[3], not_4_out, _31_26[1], _31_26[0]);
  and u_beq (beq, not_1_out, not_2_out, not_3_out, _31_26[2], not_5_out, not_6_out);
  and u_lui (lui, not_1_out, not_2_out, _31_26[3], _31_26[2], _31_26[1], _31_26[0]);
  not not_1 (not_1_out, _31_26[5]);
  not not_2 (not_2_out, _31_26[4]);
  not not_3 (not_3_out, _31_26[3]);
  not not_4 (not_4_out, _31_26[2]);
  not not_5 (not_5_out, _31_26[1]);
  not not_6 (not_6_out, _31_26[0]);
  and and_2 (special0, not_1_out, not_2_out, not_3_out, not_4_out, not_5_out, not_6_out);
  not not_7 (not_7_out, _5_0[5]);
  not not_8 (not_8_out, _5_0[4]);
  not not_9 (not_9_out, _5_0[3]);
  not not_10 (not_10_out, _5_0[2]);
  not not_11 (not_11_out, _5_0[1]);
  not not_12 (not_12_out, _5_0[0]);
  Pull_Resistor pull_resistor_1 (.node(pull_resistor_1_node));
  and add (add_out, _5_0[5], not_8_out, not_9_out, special0, not_10_out, not_11_out, not_12_out);
  and sub (sub_out, special0, _5_0[5], not_8_out, not_9_out, not_10_out, _5_0[1], not_12_out);
  or or_1 (or_1_out, add_out, lw, sw);
  Priority_Encoder #(.disabled(0)) priority_encoder_1 (
    .in0(lui), .in1(or_1_out), .in2(or_2_out), .in3(ori), .out(ALUop));  // open: in4, in5, in6, in7, en_in
  or or_2 (or_2_out, beq, sub_out);
  or or_3 (or_3_out, pull_resistor_1_node, add_out, ori);
  Priority_Encoder #(.select(2), .disabled(0)) priority_encoder_2 (
    .in0(or_3_out), .in1(or_4_out), .in2(lui), .out(EXTop));  // open: in3
  or or_4 (or_4_out, lw, sw);
  or or_5 (WDsel, add_out, sub_out, lui, ori);
  or or_6 (WRsel, lw, sw, lui, ori);
  buf or_7 (NPCop, beq);  // OR_Gate
  buf u_exttoalu (exttoalu, lui);  // OR_Gate
  buf or_8 (DMwr, sw);  // OR_Gate
  or or_9 (BSsel, lw, sw, lui, ori);
  or or_10 (RFWE, add_out, sub_out, lui, ori, lw);

  // Notes on the sheet:
  //   不能在没有或门的情况下直接上选择信号，会导致x
endmodule

module NPC (
  input  [31:0] PC,
  input  ZERO,
  input  [25:0] imm,
  input  op,
  input  [31:0] s1,
  output [31:0] nextPC,
  output [31:0] NPC
);

  wire [31:0] adder_2_out, bit_extender_1_out, multiplexer_1_out;

  Adder #(.width(32)) adder_1 (.a(32'h4), .b(PC), .out(nextPC));  // open: cin, cout
  assign bit_extender_1_out = {{14{imm[15]}}, {imm[15:0], 2'b00}};  // Bit_Extender bit_extender_1
  Adder #(.width(32)) adder_2 (.a(nextPC), .b(bit_extender_1_out), .out(adder_2_out));  // open: cin, cout
  Multiplexer #(.width(32), .enable("false")) multiplexer_1 (
    .in0(nextPC), .in1(adder_2_out), .out(multiplexer_1_out), .sel(ZERO));
  Multiplexer #(.width(32), .enable("false")) multiplexer_2 (
    .in0(nextPC), .in1(multiplexer_1_out), .out(NPC), .sel(op));
endmodule
